// Digital circuit CPU8Bit1K.dig as structural Verilog
module CPU8Bit1K (
  input  Clock,
  input  Reset,
  input  [7:0] IN,
  output [7:0] OUT
);

  wire AE, AINC, AluBMux, ARE, ARINC, BE, BINC, BusMux0, BusMux1, C, CARRY_q, CCLR, CE, CSET, E, G, INE, IRZ,
       multiplexer_1_out, N, OP0, OP1, OP2, OP3, OUTE, PCM0, PCM1, PCM2, PRomAMux, RamAMux, RamE, RamOE,
       Reserva1, Reserva2, S, Z;
  wire [1:0] A89;
  wire [5:0] IR;
  wire [7:0] A, alu8bits_1_y, B, BUS, In_q, multiplexer_3_out, PROM, ramdualport_1_d;
  wire [7:6] alu8bits_1_st;
  wire [9:0] AR, multiplexer_2_out, multiplexer_4_out, PC;

  Multiplexer #(.Selector_Bits(3)) multiplexer_1 (
    .sel({PCM2, PCM1, PCM0}), .in_0(1'b0), .in_1(1'b1), .in_2(Z), .in_3(E), .in_4(G), .in_5(S), .in_6(N),
    .in_7(C), .out(multiplexer_1_out));
  // Probe PC on PC
  // Probe BUS on BUS
  // Probe A on A
  // Probe B on B
  // Probe AR on AR
  // Probe IR on {A89, IR}
  // Probe C on C
  Reg8i A_2 (.E(AE), .INC(AINC), .CLK(Clock), .R(Reset), .D(alu8bits_1_y), .Q(A));
  BasicReg8 u_In (.Q(In_q), .D(IN), .E(INE), .CLK(Clock), .R(Reset));
  Reg10ir PC_2 (.E(multiplexer_1_out), .INC(1'b1), .nCLK(Clock), .R(Reset), .D({A89, PROM}), .Q(PC));
  ALU8Bits alu8bits_1 (
    .Y(alu8bits_1_y), .A(A), .B(multiplexer_3_out), .ST({alu8bits_1_st, C, N, S, G, E, Z}), .Cin(CARRY_q),
    .OP({OP3, OP2, OP1, OP0}));
  Multiplexer #(.Bits(10)) multiplexer_2 (.sel(PRomAMux), .in_0(PC), .in_1(AR), .out(multiplexer_2_out));
  ROM #(.AddrBits(10), .Bits(8)) u_PROM (.A(multiplexer_2_out), .sel(1'b1), .D(PROM));
  Reg8i B_2 (.E(BE), .INC(BINC), .CLK(Clock), .R(Reset), .D(BUS), .Q(B));
  Multiplexer #(.Bits(8)) multiplexer_3 (.sel(AluBMux), .in_0(BUS), .in_1(B), .out(multiplexer_3_out));
  // Probe BusMux0 on BusMux0
  // Probe BusMux1 on BusMux1
  // Probe AluBMux on AluBMux
  // Probe IRZ on IRZ
  // Probe PRomAMux on PRomAMux
  // Probe RamAMux on RamAMux
  // Probe RamOU on RamOE
  // Probe RamE on RamE
  Reg10i AR_2 (.E(ARE), .INC(ARINC), .CLK(Clock), .R(Reset), .D({A89, BUS}), .Q(AR));
  Multiplexer #(.Bits(10)) multiplexer_4 (.sel(RamAMux), .in_0(AR), .in_1({A89, PROM}), .out(multiplexer_4_out));
  RAMDualPort #(.AddrBits(10), .Bits(8)) ramdualport_1 (
    .A(multiplexer_4_out), .Din(BUS), .str(RamE), .C(Clock), .ld(RamOE), .D(ramdualport_1_d));
  BasicReg1 CARRY (.Q(CARRY_q), .S(CSET), .D(C), .E(CE), .CLK(Clock), .CLR(CCLR), .R(Reset));
  // Probe INE on INE
  Multiplexer #(.Selector_Bits(2), .Bits(8)) multiplexer_5 (
    .sel({BusMux1, BusMux0}), .in_0(alu8bits_1_y), .in_1(In_q), .in_2(PROM), .in_3(ramdualport_1_d), .out(BUS));
  // Probe OP0 on OP0
  // Probe OP1 on OP1
  // Probe OP2 on OP2
  // Probe OP3 on OP3
  // Probe PCM0 on PCM0
  // Probe PCM1 on PCM1
  // Probe PCM2 on PCM2
  BasicReg8 u_Out (.Q(OUT), .D(BUS), .E(OUTE), .CLK(Clock), .R(Reset));
  Reg8 IR_2 (.D(PROM), .Q({A89, IR}), .SR(IRZ), .nCLK(Clock), .R(Reset));
  // Probe OUTE on OUTE
  // Probe AE on AE
  // Probe AINC on AINC
  // Probe BE on BE
  // Probe BINC on BINC
  // Probe ARE on ARE
  // Probe ARINC on ARINC
  // Probe CSET on CSET
  ROM #(.AddrBits(6), .Bits(28)) Ctrl (
    .A(IR), .sel(1'b1),
    .D({Reserva2, Reserva1, CCLR, CE, CSET, ARINC, ARE, BINC, BE, AINC, AE, OUTE, INE, PCM2, PCM1, PCM0, OP3, OP2, OP1, OP0, RamE, RamOE, RamAMux, PRomAMux, IRZ, AluBMux, BusMux1, BusMux0}));
  // Probe CE on CE
  // Probe CCLR on CCLR
  // Probe Reserva1 on Reserva1
  // Probe Reserva2 on Reserva2

  // Other names for the same wires on the sheet: CLK = Clock; IR[7:6] = A89

  // Notes on the sheet:
  //   Reset: default 1
  //   contents of PROM (hex, n*v repeats v):
  //   0,1,a,2,b,43,33,4,2,aa,5,6,2,b,7,1,1a,2,1b,8,a1,9,b1,48,a2,49,b2
  //   Version 0.2
  //   contents of Ctrl (hex, n*v repeats v):
  //   0,2010a,8000a,20000a,80000,20104,80,184,a0,1a4
endmodule
